// Logisim project ULA.circ as structural Verilog: 8 circuits, main circuit main
module main (
);

  _5bit_adder u_5bit_adder_1 ();  // open: D5, D4, D3, D2, D1, m, B1, A1, B2, A2, B3, A3, B4, A4, B5, A5
endmodule

module half_adder (
  input  A,
  input  B,
  output Carry_out,
  output Soma
);

  and and_1 (Carry_out, B, A);
  xor xor_1 (Soma, A, B);
endmodule

module full_adder (
  input  A,
  input  B,
  input  Carry_in,
  output Carry_out,
  output Soma
);

  wire half_adder_2_carry_out, half_adder_carry_out, half_adder_soma;

  half_adder half_adder (.A(A), .B(B), .Carry_out(half_adder_carry_out), .Soma(half_adder_soma));
  half_adder half_adder_2 (.A(half_adder_soma), .B(Carry_in), .Carry_out(half_adder_2_carry_out), .Soma(Soma));
  or or_1 (Carry_out, half_adder_carry_out, half_adder_2_carry_out);
endmodule

module C2_format (
  input  M,
  input  D1,
  input  D2,
  input  D3,
  input  D4,
  input  D5,
  input  in_7,
  output out_8,
  output out_9,
  output out_10,
  output out_11,
  output out_12
);

  wire full_adder_1_carry_out, full_adder_2_carry_out, full_adder_3_carry_out, full_adder_4_carry_out,
       not_1_out, not_2_out, not_3_out, not_4_out, not_5_out, not_6_out, xor_1_out, xor_2_out, xor_3_out,
       xor_4_out, xor_5_out;

  not not_1 (not_1_out, D1);
  not not_2 (not_2_out, D2);
  not not_3 (not_3_out, D3);
  not not_4 (not_4_out, D4);
  not not_5 (not_5_out, D5);
  not not_6 (not_6_out, M);
  xor xor_1 (xor_1_out, not_1_out, M);
  xor xor_2 (xor_2_out, not_2_out, M);
  xor xor_3 (xor_3_out, not_3_out, M);
  xor xor_4 (xor_4_out, not_4_out, M);
  xor xor_5 (xor_5_out, not_5_out, M);
  full_adder full_adder_1 (
    .A(xor_1_out), .B(not_6_out), .Carry_in(in_7), .Carry_out(full_adder_1_carry_out), .Soma(out_8));
  full_adder full_adder_2 (
    .A(xor_2_out), .B(in_7), .Carry_in(full_adder_1_carry_out), .Carry_out(full_adder_2_carry_out),
    .Soma(out_9));
  full_adder full_adder_3 (
    .A(xor_3_out), .B(in_7), .Carry_in(full_adder_2_carry_out), .Carry_out(full_adder_3_carry_out),
    .Soma(out_10));
  full_adder full_adder_4 (
    .A(xor_4_out), .B(in_7), .Carry_in(full_adder_3_carry_out), .Carry_out(full_adder_4_carry_out),
    .Soma(out_11));
  full_adder full_adder_5 (
    .A(xor_5_out), .B(in_7), .Carry_in(full_adder_4_carry_out), .Soma(out_12));  // open: Carry_out
endmodule

module _1bit_comparator (
  input  A,
  input  B,
  input  in_equal,
  input  in_greater_than,
  input  in_less_than,
  output A___B,
  output A___B_2,
  output A___B_3
);

  wire and_1_out, and_2_out, not_1_out, not_2_out, xnor_1_out;

  not not_1 (not_1_out, B);
  not not_2 (not_2_out, A);
  xnor xnor_1 (xnor_1_out, A, B);
  and and_1 (and_1_out, A, in_equal, not_1_out);
  and and_2 (and_2_out, not_2_out, in_equal, B);
  and and_3 (A___B, xnor_1_out, in_equal);
  or or_1 (A___B_2, in_greater_than, and_1_out);
  or or_2 (A___B_3, in_less_than, and_2_out);
endmodule

module _5bit_comparator (
  input  left_less,
  input  left_greater,
  input  left_equal,
  input  B5,
  input  A5,
  input  B4,
  input  A4,
  input  B3,
  input  A3,
  input  B2,
  input  A2,
  input  B1,
  input  A1,
  output out_14,
  output out_15,
  output out_16
);

  wire n1bit_comparator_1_a___b, n1bit_comparator_1_a___b_2, n1bit_comparator_1_a___b_3,
       n1bit_comparator_2_a___b, n1bit_comparator_2_a___b_2, n1bit_comparator_2_a___b_3,
       n1bit_comparator_3_a___b, n1bit_comparator_3_a___b_2, n1bit_comparator_3_a___b_3,
       n1bit_comparator_4_a___b, n1bit_comparator_4_a___b_2, n1bit_comparator_4_a___b_3, not_1_out, not_2_out;

  _1bit_comparator u_1bit_comparator_1 (
    .A(not_2_out), .B(not_1_out), .in_equal(left_equal), .in_greater_than(left_greater),
    .in_less_than(left_less), .A___B(n1bit_comparator_1_a___b), .A___B_2(n1bit_comparator_1_a___b_2),
    .A___B_3(n1bit_comparator_1_a___b_3));
  _1bit_comparator u_1bit_comparator_2 (
    .A(A4), .B(B4), .in_equal(n1bit_comparator_1_a___b), .in_greater_than(n1bit_comparator_1_a___b_2),
    .in_less_than(n1bit_comparator_1_a___b_3), .A___B(n1bit_comparator_2_a___b),
    .A___B_2(n1bit_comparator_2_a___b_2), .A___B_3(n1bit_comparator_2_a___b_3));
  _1bit_comparator u_1bit_comparator_3 (
    .A(A3), .B(B3), .in_equal(n1bit_comparator_2_a___b), .in_greater_than(n1bit_comparator_2_a___b_2),
    .in_less_than(n1bit_comparator_2_a___b_3), .A___B(n1bit_comparator_3_a___b),
    .A___B_2(n1bit_comparator_3_a___b_2), .A___B_3(n1bit_comparator_3_a___b_3));
  _1bit_comparator u_1bit_comparator_4 (
    .A(A2), .B(B2), .in_equal(n1bit_comparator_3_a___b), .in_greater_than(n1bit_comparator_3_a___b_2),
    .in_less_than(n1bit_comparator_3_a___b_3), .A___B(n1bit_comparator_4_a___b),
    .A___B_2(n1bit_comparator_4_a___b_2), .A___B_3(n1bit_comparator_4_a___b_3));
  not not_1 (not_1_out, B5);
  not not_2 (not_2_out, A5);
  _1bit_comparator u_1bit_comparator_5 (
    .A(A1), .B(B1), .in_equal(n1bit_comparator_4_a___b), .in_greater_than(n1bit_comparator_4_a___b_2),
    .in_less_than(n1bit_comparator_4_a___b_3), .A___B(out_16), .A___B_2(out_15), .A___B_3(out_14));
endmodule

module _5bit_adder (
  input  m,
  input  B1,
  input  A1,
  input  B2,
  input  A2,
  input  B3,
  input  A3,
  input  B4,
  input  A4,
  input  B5,
  input  A5,
  output D5,
  output D4,
  output D3,
  output D2,
  output D1
);

  wire full_adder_2_carry_out, full_adder_3_carry_out, full_adder_4_carry_out, full_adder_5_carry_out;

  full_adder full_adder_1 (.A(A5), .B(B5), .Carry_in(full_adder_2_carry_out), .Soma(D5));  // open: Carry_out
  full_adder full_adder_2 (
    .A(A4), .B(B4), .Carry_in(full_adder_3_carry_out), .Carry_out(full_adder_2_carry_out), .Soma(D4));
  full_adder full_adder_3 (
    .A(A3), .B(B3), .Carry_in(full_adder_5_carry_out), .Carry_out(full_adder_3_carry_out), .Soma(D3));
  full_adder full_adder_4 (.A(A1), .B(B1), .Carry_in(m), .Carry_out(full_adder_4_carry_out), .Soma(D1));
  full_adder full_adder_5 (
    .A(A2), .B(B2), .Carry_in(full_adder_4_carry_out), .Carry_out(full_adder_5_carry_out), .Soma(D2));
endmodule

module _5bit_subtractor (
  input  m,
  input  B1,
  input  A1,
  input  B2,
  input  A2,
  input  B3,
  input  A3,
  input  B4,
  input  A4,
  input  B5,
  input  A5,
  output D5,
  output D4,
  output D3,
  output D2,
  output D1
);

  wire full_adder_1_carry_out, full_adder_3_carry_out, full_adder_4_carry_out, full_adder_5_carry_out,
       xor_1_out, xor_2_out, xor_3_out, xor_4_out, xor_5_out;

  full_adder full_adder_1 (
    .A(A4), .B(xor_4_out), .Carry_in(full_adder_3_carry_out), .Carry_out(full_adder_1_carry_out), .Soma(D4));
  full_adder full_adder_2 (.A(A5), .B(xor_5_out), .Carry_in(full_adder_1_carry_out), .Soma(D5));  // open: Carry_out
  full_adder full_adder_3 (
    .A(A3), .B(xor_3_out), .Carry_in(full_adder_5_carry_out), .Carry_out(full_adder_3_carry_out), .Soma(D3));
  full_adder full_adder_4 (.A(A1), .B(xor_1_out), .Carry_in(m), .Carry_out(full_adder_4_carry_out), .Soma(D1));
  full_adder full_adder_5 (
    .A(A2), .B(xor_2_out), .Carry_in(full_adder_4_carry_out), .Carry_out(full_adder_5_carry_out), .Soma(D2));
  xor xor_1 (xor_1_out, B1, m);
  xor xor_2 (xor_2_out, B2, m);
  xor xor_3 (xor_3_out, B3, m);
  xor xor_4 (xor_4_out, B4, m);
  xor xor_5 (xor_5_out, B5, m);
endmodule
